// Logisim project lab08part3-jam433.circ as structural Verilog: 1 circuit, main circuit main
module main (
  input  A,
  input  B,
  input  C,
  output V
);

  wire A_n_BC_out, n_AB_C_out, n_AB_out, n_ABC_out, n_AC_out, n_BC_out, nAB_nC_out, not_1_out, not_2_out,
       not_3_out, O1_out, O2_out;

  not not_1 (not_1_out, A);
  not not_2 (not_2_out, B);
  not not_3 (not_3_out, C);
  and n_AB (n_AB_out, not_1_out, not_2_out);
  and n_BC (n_BC_out, not_2_out, not_3_out);
  and n_AC (n_AC_out, not_1_out, not_3_out);
  and n_ABC (n_ABC_out, not_3_out, n_AB_out);
  and n_AB_C (n_AB_C_out, C, n_AB_out);
  and A_n_BC (A_n_BC_out, A, n_BC_out);
  and nAB_nC (nAB_nC_out, B, n_AC_out);
  or O1 (O1_out, n_ABC_out, n_AB_C_out);
  or O2 (O2_out, A_n_BC_out, nAB_nC_out);
  or O3 (V, O1_out, O2_out);
endmodule
