// Logisim project lab10part2-jam433.circ as structural Verilog: 1 circuit, main circuit main
module main (
  input  [3:0] in_1
);

  wire clock_1_out, comparator_1_gt, controlled_buffer_1_out, Reset_out;
  wire [3:0] counter_1_q, ram_1_data, register_1_q;

  Clock clock_1 (.out(clock_1_out));
  Button Reset (.out(Reset_out));
  Register #(.width(4)) register_1 (.D(counter_1_q), .Q(register_1_q), .clk(clock_1_out), .clr(Reset_out));  // open: en
  Comparator #(.width(4), .mode("unsigned")) comparator_1 (
    .a(in_1), .b(register_1_q), .gt(comparator_1_gt));  // open: eq, lt
  RAM #(.addrWidth(4), .dataWidth(4), .bus("separate")) ram_1 (
    .addr(register_1_q), .din(register_1_q), .data(ram_1_data), .clk(clock_1_out), .clr(Reset_out));  // open: str, sel, ld
  assign controlled_buffer_1_out = comparator_1_gt ? clock_1_out : 1'bz;  // Controlled_Buffer controlled_buffer_1
  Counter #(.width(4), .max('hf)) counter_1 (
    .D(ram_1_data), .Q(counter_1_q), .clk(controlled_buffer_1_out), .clr(Reset_out));  // open: load, count, carry
endmodule
