// Logisim project lab12-jam433.circ as structural Verilog: 4 circuits, main circuit main
module main (
);

  wire clock_1_out, decoder_select, Fields_reg, not_1_out;
  wire [1:0] decoder_op;
  wire [3:0] Fields_opcode;
  wire [7:0] adder_1_out, ALU_result, Fields_imm, multiplexer_1_out, register_1_q, register_2_q, register_3_q;
  wire [15:0] rom_1_data;

  Adder adder_1 (.a(8'h1), .b(register_1_q), .out(adder_1_out));  // open: cin, cout
  Register register_1 (.D(adder_1_out), .en(1'b1), .Q(register_1_q), .clk(clock_1_out));  // open: clr
  Clock clock_1 (.out(clock_1_out));
  ROM #(.dataWidth(16)) rom_1 (.addr(register_1_q), .data(rom_1_data), .sel(1'b1));
  fields Fields (.instruction(rom_1_data), .imm(Fields_imm), .\reg (Fields_reg), .opcode(Fields_opcode));
  not not_1 (not_1_out, Fields_reg);
  Register register_2 (.D(multiplexer_1_out), .en(not_1_out), .Q(register_2_q), .clk(clock_1_out));  // open: clr
  Register register_3 (.D(multiplexer_1_out), .en(Fields_reg), .Q(register_3_q), .clk(clock_1_out));  // open: clr
  decoder decoder (.op_code(Fields_opcode), .op(decoder_op), .select(decoder_select));
  ALU ALU (.A(register_2_q), .B(register_3_q), .Operation(decoder_op), .Result(ALU_result));
  Multiplexer #(.width(8), .enable("false")) multiplexer_1 (
    .in0(ALU_result), .in1(Fields_imm), .out(multiplexer_1_out), .sel(decoder_select));

  // Notes on the sheet:
  //   contents of rom_1 (hex, n*v repeats v):
  //   1 802
endmodule

module ALU (
  input  [7:0] A,
  input  [7:0] B,
  input  [1:0] Operation,
  output [7:0] Result
);

  wire [7:0] adder_1_out, and_1_out, nor_1_out, subtractor_1_out;

  Adder adder_1 (.a(A), .b(B), .out(adder_1_out), .cin(1'b0));  // open: cout
  Subtractor subtractor_1 (.a(A), .b(B), .out(subtractor_1_out), .bin(1'b0));  // open: bout
  assign nor_1_out = ~(A | B);  // NOR_Gate nor_1, 8 bits wide
  assign and_1_out = A & B;  // AND_Gate and_1, 8 bits wide
  Multiplexer #(.select(2), .width(8), .enable("false")) multiplexer_1 (
    .in0(adder_1_out), .in1(subtractor_1_out), .in2(nor_1_out), .in3(and_1_out), .out(Result), .sel(Operation));
endmodule

module fields (
  input  [15:0] instruction,
  output [7:0] imm,
  output \reg ,
  output [3:0] opcode
);


  assign imm = instruction[7:0];
  assign opcode = instruction[15:12];
  assign \reg  = instruction[11];
endmodule

module decoder (
  input  [3:0] op_code,
  output [1:0] op,
  output select
);

  wire not_1_out, not_2_out;

  not not_1 (not_1_out, op_code[2]);
  not not_2 (not_2_out, op_code[3]);
  and and_1 (select, not_1_out, not_2_out);

  assign op = {op_code[3], op_code[0]};
endmodule
