// Logisim project jrmips.circ as structural Verilog: 8 circuits, main circuit main
module main (
);

  wire ALU_src, and_1_out, branch, branch_logic_branch_out, clock, decoder_1_halt, decoder_1_put, jump,
       mem_read, mem_reg, mem_write, not_1_out, not_2_out, or_1_out, or_2_out, reg_write, shift, sub_OP;
  wire [2:0] ALU_OP, Rs;
  wire [3:0] OP_code;
  wire [7:0] Imm, multiplexer_2_out, PC_1, PC_out, PC_q;
  wire [15:0] ALU_result, multiplexer_3_out, multiplexer_5_out, multiplexer_6_out, ram_1_data, register_1_q,
       Rs_data, Rt_data, shift_logical, sign_ext_output, sign_extend_1_output, write_data;

  not not_1 (not_1_out, decoder_1_halt);
  Register PC (.D(PC_out), .en(not_1_out), .Q(PC_q), .clk(clock));  // open: clr
  LED HALT (.in(decoder_1_halt));
  Clock clock_1 (.out(clock));
  Adder adder_1 (.a(8'h1), .b(PC_q), .out(PC_1));  // open: cin, cout
  ROM #(.dataWidth(16)) rom_1 (.addr(PC_q), .data({OP_code, Rs, Imm, sub_OP}), .sel(1'b1));
  decoder decoder_1 (
    .OP_3(OP_code[3]), .jump(jump), .OP_2(OP_code[2]), .OP_1(OP_code[1]), .shift(shift), .OP_0(OP_code[0]),
    .branch(branch), .Sub_OP(sub_OP), .mem_to_reg(mem_reg), .reg_write(reg_write), .mem_write(mem_write),
    .mem_read(mem_read), .ALU_src(ALU_src), .ALU_2(ALU_OP[2]), .ALU_1(ALU_OP[1]), .ALU_0(ALU_OP[0]),
    .put(decoder_1_put), .halt(decoder_1_halt));
  Register #(.width(16)) register_1 (.D(Rs_data), .en(decoder_1_put), .Q(register_1_q), .clk(clock));  // open: clr
  branch_logic branch_logic (.Rs(Rs_data), .sub_op(sub_OP), .op_code(OP_code), .branch_out(branch_logic_branch_out));
  or or_1 (or_1_out, branch_logic_branch_out, jump);
  Hex_Digit_Display hex_digit_display_1 (.value(register_1_q[15:12]));  // open: dp
  Hex_Digit_Display hex_digit_display_2 (.value(register_1_q[11:8]));  // open: dp
  Hex_Digit_Display hex_digit_display_3 (.value(register_1_q[7:4]));  // open: dp
  Hex_Digit_Display hex_digit_display_4 (.value(register_1_q[3:0]));  // open: dp
  Multiplexer #(.width(8), .enable("false")) multiplexer_1 (
    .in0(PC_1), .in1(multiplexer_2_out), .out(PC_out), .sel(or_2_out));
  and and_1 (and_1_out, branch, or_1_out);
  or or_2 (or_2_out, and_1_out, jump);
  reg_file reg_file (
    .to_write(Rs), .read_data_1(Rs_data), .read_1(Rs), .read_data_2(Rt_data), .read_2(Imm[7:5]),
    .Clock(clock), .reg_write(reg_write), .write_data(write_data));
  Multiplexer #(.width(8), .enable("false")) multiplexer_2 (
    .in0(Rs_data[7:0]), .in1(Imm), .out(multiplexer_2_out), .sel(not_2_out));
  sign_extend sign_ext (.Input(Imm), .sub_OP(sub_OP), .Output(sign_ext_output));
  Multiplexer #(.width(16), .enable("false")) multiplexer_3 (
    .in0(Rt_data), .in1(sign_ext_output), .out(multiplexer_3_out), .sel(ALU_src));
  Multiplexer #(.width(16), .enable("false")) multiplexer_4 (
    .in0(multiplexer_5_out), .in1(shift_logical), .out(write_data), .sel(shift));
  ALU ALU (.Input_A(Rs_data), .Input_B(multiplexer_3_out), .ALU_Result(ALU_result), .OpCode(ALU_OP));
  not not_2 (not_2_out, jump);
  Multiplexer #(.width(16), .enable("false")) multiplexer_5 (
    .in0(multiplexer_6_out), .in1(sign_extend_1_output), .out(multiplexer_5_out), .sel(jump));
  sign_extend sign_extend_1 (.Input(PC_1), .sub_OP(1'b0), .Output(sign_extend_1_output));
  RAM #(.dataWidth(16), .bus("separate")) ram_1 (
    .addr(Rt_data[7:0]), .din(Rs_data), .data(ram_1_data), .str(mem_write), .sel(1'b1), .clk(clock),
    .ld(mem_read));  // open: clr
  Multiplexer #(.width(16), .enable("false")) multiplexer_6 (
    .in0(ALU_result), .in1(ram_1_data), .out(multiplexer_6_out), .sel(mem_reg));
  shift_logic shift_logic (.Rs(Rs_data), .Shamt(Imm[3:0]), .Rt(Rt_data), .Sub_OP(sub_OP), .shift_output(shift_logical));

  // Other names for the same wires on the sheet: shamt[3:0] = Imm[3:0]; Rt[2:0] = Imm[7:5]

  // Notes on the sheet:
  //   Jamie Min
  //   jam433@pitt.edu
  //   contents of rom_1 (hex, n*v repeats v):
  //   8200 7440 2680 15fe 6404 8202 7641 7840 b800 b001
endmodule

module reg_file (
  input  [2:0] read_1,
  input  reg_write,
  input  [2:0] to_write,
  input  [2:0] read_2,
  input  [15:0] write_data,
  input  Clock,
  output [15:0] read_data_1,
  output [15:0] read_data_2
);

  wire demultiplexer_1_out0, demultiplexer_1_out1, demultiplexer_1_out2, demultiplexer_1_out3,
       demultiplexer_1_out4, demultiplexer_1_out5, demultiplexer_1_out6, demultiplexer_1_out7;
  wire [15:0] r0_q, r1_q, r2_q, r3_q, r4_q, r5_q, r6_q, r7_q;

  Demultiplexer #(.select(3), .disabled(0)) demultiplexer_1 (
    .out0(demultiplexer_1_out0), .out1(demultiplexer_1_out1), .out2(demultiplexer_1_out2),
    .out3(demultiplexer_1_out3), .out4(demultiplexer_1_out4), .out5(demultiplexer_1_out5),
    .out6(demultiplexer_1_out6), .out7(demultiplexer_1_out7), .in(1'b1), .sel(to_write), .en(reg_write));
  Register #(.width(16)) r0 (.D(write_data), .en(demultiplexer_1_out0), .Q(r0_q), .clk(Clock));  // open: clr
  Register #(.width(16)) r1 (.D(write_data), .en(demultiplexer_1_out1), .Q(r1_q), .clk(Clock));  // open: clr
  Register #(.width(16)) r2 (.D(write_data), .en(demultiplexer_1_out2), .Q(r2_q), .clk(Clock));  // open: clr
  Register #(.width(16)) r3 (.D(write_data), .en(demultiplexer_1_out3), .Q(r3_q), .clk(Clock));  // open: clr
  Register #(.width(16)) r4 (.D(write_data), .en(demultiplexer_1_out4), .Q(r4_q), .clk(Clock));  // open: clr
  Register #(.width(16)) r5 (.D(write_data), .en(demultiplexer_1_out5), .Q(r5_q), .clk(Clock));  // open: clr
  Register #(.width(16)) r6 (.D(write_data), .en(demultiplexer_1_out6), .Q(r6_q), .clk(Clock));  // open: clr
  Register #(.width(16)) r7 (.D(write_data), .en(demultiplexer_1_out7), .Q(r7_q), .clk(Clock));  // open: clr
  Multiplexer #(.select(3), .width(16), .enable("false")) multiplexer_1 (
    .in0(r0_q), .in1(r1_q), .in2(r2_q), .in3(r3_q), .in4(r4_q), .in5(r5_q), .in6(r6_q), .in7(r7_q),
    .out(read_data_1), .sel(read_1));
  Multiplexer #(.select(3), .width(16), .enable("false")) multiplexer_2 (
    .in0(r0_q), .in1(r1_q), .in2(r2_q), .in3(r3_q), .in4(r4_q), .in5(r5_q), .in6(r6_q), .in7(r7_q),
    .out(read_data_2), .sel(read_2));
endmodule

module ALU (
  input  [15:0] Input_A,
  input  [15:0] Input_B,
  input  [2:0] OpCode,
  output [15:0] ALU_Result
);

  wire [15:0] adder_1_out, and_1_out, divider_1_out, multiplier_1_out, nor_1_out, subtractor_1_out;

  assign and_1_out = Input_A & Input_B;  // AND_Gate and_1, 16 bits wide
  assign nor_1_out = ~(Input_B | Input_A);  // NOR_Gate nor_1, 16 bits wide
  Adder #(.width(16)) adder_1 (.a(Input_A), .b(Input_B), .out(adder_1_out));  // open: cin, cout
  Subtractor #(.width(16)) subtractor_1 (.a(Input_A), .b(Input_B), .out(subtractor_1_out));  // open: bin, bout
  Divider #(.width(16)) divider_1 (.a(Input_A), .b(Input_B), .out(divider_1_out));  // open: upper, rem
  Multiplier #(.width(16)) multiplier_1 (.a(Input_A), .b(Input_B), .out(multiplier_1_out));  // open: cin, cout
  Multiplexer #(.select(3), .width(16), .enable("false")) multiplexer_1 (
    .in0(and_1_out), .in1(nor_1_out), .in2(adder_1_out), .in3(subtractor_1_out), .in4(divider_1_out),
    .in5(multiplier_1_out), .out(ALU_Result), .sel(OpCode));  // open: in6, in7
endmodule

module R_I_decoder (
  input  OP_0,
  input  OP_1,
  input  OP_2,
  input  OP_3,
  input  Sub_OP,
  output instructionFormat
);

  wire and_1_out, and_2_out, and_3_out, and_4_out, and_5_out, not_1_out, not_2_out, not_3_out, not_4_out,
       not_5_out, not_6_out, not_7_out, not_8_out, not_9_out;

  not not_1 (not_1_out, OP_0);
  not not_2 (not_2_out, OP_2);
  not not_3 (not_3_out, OP_2);
  not not_4 (not_4_out, Sub_OP);
  not not_5 (not_5_out, OP_2);
  not not_6 (not_6_out, OP_0);
  not not_7 (not_7_out, OP_3);
  not not_8 (not_8_out, OP_1);
  not not_9 (not_9_out, OP_3);
  and and_1 (and_1_out, not_1_out, not_2_out, OP_3);
  and and_2 (and_2_out, not_3_out, OP_3, not_4_out);
  and and_3 (and_3_out, OP_1, not_5_out, OP_3);
  and and_4 (and_4_out, not_6_out, OP_1, OP_2, not_7_out);
  and and_5 (and_5_out, OP_0, not_8_out, not_9_out);
  or or_1 (instructionFormat, and_1_out, and_2_out, and_3_out, and_4_out, and_5_out);

  // Notes on the sheet:
  //   0 = R
  //   1 = I
endmodule

module decoder (
  input  OP_3,
  input  OP_2,
  input  OP_1,
  input  OP_0,
  input  Sub_OP,
  output jump,
  output shift,
  output branch,
  output mem_to_reg,
  output reg_write,
  output mem_write,
  output mem_read,
  output ALU_src,
  output ALU_2,
  output ALU_1,
  output ALU_0,
  output put,
  output halt
);

  wire and_2_out, and_3_out, and_5_out, and_6_out, and_8_out, and_9_out, and_10_out, and_12_out, and_13_out,
       and_14_out, and_15_out, and_17_out, and_18_out, and_19_out, and_20_out, and_21_out, and_22_out,
       and_23_out, not_1_out, not_2_out, not_3_out, not_4_out, not_5_out, not_6_out, not_7_out, not_8_out,
       not_9_out, not_10_out, not_11_out, not_12_out, not_13_out, not_14_out, not_15_out, not_16_out,
       not_17_out, not_18_out, not_19_out, not_20_out, not_21_out, not_22_out, not_23_out, not_24_out,
       not_25_out, not_26_out, not_27_out, not_28_out, not_29_out, not_30_out, not_31_out, not_32_out,
       not_33_out, not_34_out, not_35_out, not_36_out, not_37_out, not_38_out;

  not not_1 (not_1_out, OP_1);
  not not_2 (not_2_out, OP_0);
  not not_3 (not_3_out, OP_1);
  not not_4 (not_4_out, OP_0);
  not not_5 (not_5_out, OP_1);
  not not_6 (not_6_out, OP_0);
  not not_7 (not_7_out, Sub_OP);
  not not_8 (not_8_out, OP_3);
  not not_9 (not_9_out, OP_2);
  not not_10 (not_10_out, OP_1);
  not not_11 (not_11_out, OP_0);
  not not_12 (not_12_out, OP_3);
  not not_13 (not_13_out, Sub_OP);
  and and_1 (mem_write, OP_2, OP_1, OP_0, Sub_OP);
  not not_14 (not_14_out, Sub_OP);
  not not_15 (not_15_out, OP_3);
  not not_16 (not_16_out, OP_1);
  not not_17 (not_17_out, OP_0);
  not not_18 (not_18_out, OP_1);
  not not_19 (not_19_out, Sub_OP);
  not not_20 (not_20_out, OP_0);
  not not_21 (not_21_out, OP_3);
  not not_22 (not_22_out, OP_2);
  not not_23 (not_23_out, OP_3);
  not not_24 (not_24_out, OP_2);
  not not_25 (not_25_out, OP_1);
  not not_26 (not_26_out, OP_3);
  not not_27 (not_27_out, OP_2);
  not not_28 (not_28_out, OP_0);
  not not_29 (not_29_out, OP_1);
  not not_30 (not_30_out, OP_0);
  not not_31 (not_31_out, OP_1);
  not not_32 (not_32_out, OP_0);
  not not_33 (not_33_out, OP_3);
  not not_34 (not_34_out, OP_1);
  not not_35 (not_35_out, OP_0);
  not not_36 (not_36_out, OP_3);
  not not_37 (not_37_out, OP_2);
  not not_38 (not_38_out, Sub_OP);
  and and_2 (and_2_out, OP_3, not_1_out, OP_0);
  and and_3 (and_3_out, OP_3, OP_1, not_2_out);
  and and_4 (shift, OP_2, not_3_out, not_4_out);
  and and_5 (and_5_out, OP_2, not_5_out, OP_0);
  and and_6 (and_6_out, OP_2, OP_1, not_6_out);
  and and_7 (mem_to_reg, OP_2, OP_1, not_7_out);
  and and_8 (and_8_out, not_8_out, not_9_out);
  and and_9 (and_9_out, not_10_out, not_11_out);
  and and_10 (and_10_out, not_12_out, OP_1, OP_0, not_13_out);
  and and_11 (mem_read, OP_2, OP_1, OP_0, not_14_out);
  and and_12 (and_12_out, not_15_out, not_16_out, OP_0);
  and and_13 (and_13_out, OP_2, OP_1, not_17_out);
  and and_14 (and_14_out, OP_3, not_18_out, not_19_out);
  and and_15 (and_15_out, OP_3, not_20_out);
  and and_16 (ALU_2, not_21_out, not_22_out, OP_1, OP_0);
  and and_17 (and_17_out, not_23_out, not_24_out, not_25_out, OP_0);
  and and_18 (and_18_out, not_26_out, not_27_out, OP_1, not_28_out);
  and and_19 (and_19_out, OP_2, not_29_out, not_30_out);
  and and_20 (and_20_out, OP_2, OP_1, OP_0);
  and and_21 (and_21_out, OP_3, not_31_out, not_32_out);
  and and_22 (and_22_out, not_33_out, not_34_out, not_35_out, Sub_OP);
  and and_23 (and_23_out, not_36_out, not_37_out, OP_1, Sub_OP);
  and and_24 (put, OP_3, OP_1, OP_0, not_38_out);
  and and_25 (halt, OP_3, OP_1, OP_0, Sub_OP);
  or or_1 (jump, and_2_out, and_3_out);
  or or_2 (branch, and_5_out, and_6_out);
  or or_3 (reg_write, and_8_out, and_9_out, and_10_out);
  or or_4 (ALU_src, and_12_out, and_13_out, and_14_out, and_15_out);
  or or_5 (ALU_1, and_17_out, and_18_out, and_19_out, and_20_out, and_21_out);
  or or_6 (ALU_0, and_22_out, and_23_out);
endmodule

module sign_extend (
  input  [7:0] Input,
  input  sub_OP,
  output [15:0] Output
);

  wire not_1_out;
  wire [15:0] bit_extender_1_out, bit_extender_2_out;

  assign bit_extender_1_out = {{8{1'b0}}, Input};  // Bit_Extender bit_extender_1
  assign bit_extender_2_out = {{8{Input[7]}}, Input};  // Bit_Extender bit_extender_2
  not not_1 (not_1_out, sub_OP);
  Multiplexer #(.width(16), .enable("false")) multiplexer_1 (
    .in0(bit_extender_1_out), .in1(bit_extender_2_out), .out(Output), .sel(not_1_out));
endmodule

module shift_logic (
  input  [15:0] Rs,
  input  [3:0] Shamt,
  input  [15:0] Rt,
  input  Sub_OP,
  output [15:0] shift_output
);

  wire [3:0] multiplexer_1_out;
  wire [15:0] shifter_1_out, shifter_2_out;

  Multiplexer #(.width(4), .enable("false")) multiplexer_1 (
    .in0(Shamt), .in1(Rt[3:0]), .out(multiplexer_1_out), .sel(Sub_OP));
  Shifter #(.width(16)) shifter_1 (.in(Rs), .\dist (multiplexer_1_out), .out(shifter_1_out));
  Shifter #(.width(16), .shift("lr")) shifter_2 (.in(Rs), .\dist (multiplexer_1_out), .out(shifter_2_out));
  Multiplexer #(.width(16), .enable("false")) multiplexer_2 (
    .in0(shifter_1_out), .in1(shifter_2_out), .out(shift_output), .sel(Sub_OP));
endmodule

module branch_logic (
  input  [15:0] Rs,
  input  sub_op,
  input  [3:0] op_code,
  output branch_out
);

  wire comparator_1_eq, comparator_1_gt, comparator_1_lt, not_1_out;

  Comparator #(.width(16)) comparator_1 (
    .a(Rs), .b({16{1'b0}}), .gt(comparator_1_gt), .eq(comparator_1_eq), .lt(comparator_1_lt));
  not not_1 (not_1_out, comparator_1_eq);
  Multiplexer #(.select(2), .enable("false")) multiplexer_1 (
    .in0(not_1_out), .in1(comparator_1_eq), .in2(comparator_1_gt), .in3(comparator_1_lt), .out(branch_out),
    .sel({op_code[1], sub_op}));
endmodule
