// Logisim project lab09part1-jam433.circ as structural Verilog: 1 circuit, main circuit main
module main (
  input  A1,
  input  A0,
  input  B1,
  input  B0,
  output out_5
);

  wire and_1_out, and_2_out, and_3_out, not_1_out, not_2_out, not_3_out, not_4_out;

  not not_1 (not_1_out, A1);
  not not_2 (not_2_out, A0);
  not not_3 (not_3_out, B1);
  not not_4 (not_4_out, B0);
  and and_1 (and_1_out, A1, not_3_out);
  and and_2 (and_2_out, not_3_out, not_4_out);
  and and_3 (and_3_out, A1, not_4_out);
  or or_1 (out_5, and_1_out, and_2_out, and_3_out);
endmodule
