// Logisim project lab09part2-jam433.circ as structural Verilog: 2 circuits, main circuit main
module main (
);

  wire Batch1_out, Batch2_out, Batch3_2_out, Batch3_out, Batch4_out, Batch5_out, Clock_out,
       cookiewatcher_1_cookiesburnt, cookiewatcher_1_cookiesdone, cookiewatcher_2_cookiesburnt,
       cookiewatcher_2_cookiesdone, cookiewatcher_3_cookiesburnt, cookiewatcher_3_cookiesdone,
       cookiewatcher_4_cookiesburnt, cookiewatcher_4_cookiesdone, cookiewatcher_5_cookiesburnt,
       cookiewatcher_5_cookiesdone, cookiewatcher_6_cookiesburnt, cookiewatcher_6_cookiesdone;

  Clock Clock (.out(Clock_out));
  Button Batch1 (.out(Batch1_out));
  Button Batch2 (.out(Batch2_out));
  Button Batch3 (.out(Batch3_out));
  Button Batch3_2 (.out(Batch3_2_out));
  Button Batch4 (.out(Batch4_out));
  Button Batch5 (.out(Batch5_out));
  CookieWatcher cookiewatcher_1 (
    .Clock(Clock_out), .BatchHandled(Batch1_out), .CookiesBurnt(cookiewatcher_1_cookiesburnt),
    .CookiesDone(cookiewatcher_1_cookiesdone));
  CookieWatcher cookiewatcher_2 (
    .Clock(Clock_out), .BatchHandled(Batch2_out), .CookiesBurnt(cookiewatcher_2_cookiesburnt),
    .CookiesDone(cookiewatcher_2_cookiesdone));
  CookieWatcher cookiewatcher_3 (
    .Clock(Clock_out), .BatchHandled(Batch3_out), .CookiesBurnt(cookiewatcher_3_cookiesburnt),
    .CookiesDone(cookiewatcher_3_cookiesdone));
  CookieWatcher cookiewatcher_4 (
    .Clock(Clock_out), .BatchHandled(Batch3_2_out), .CookiesBurnt(cookiewatcher_4_cookiesburnt),
    .CookiesDone(cookiewatcher_4_cookiesdone));
  CookieWatcher cookiewatcher_5 (
    .Clock(Clock_out), .BatchHandled(Batch4_out), .CookiesBurnt(cookiewatcher_5_cookiesburnt),
    .CookiesDone(cookiewatcher_5_cookiesdone));
  CookieWatcher cookiewatcher_6 (
    .Clock(Clock_out), .BatchHandled(Batch5_out), .CookiesBurnt(cookiewatcher_6_cookiesburnt),
    .CookiesDone(cookiewatcher_6_cookiesdone));
  LED led_1 (.in(cookiewatcher_1_cookiesburnt));
  LED led_2 (.in(cookiewatcher_1_cookiesdone));
  LED led_3 (.in(cookiewatcher_2_cookiesburnt));
  LED led_4 (.in(cookiewatcher_2_cookiesdone));
  LED led_5 (.in(cookiewatcher_3_cookiesburnt));
  LED led_6 (.in(cookiewatcher_3_cookiesdone));
  LED led_7 (.in(cookiewatcher_4_cookiesburnt));
  LED led_8 (.in(cookiewatcher_4_cookiesdone));
  LED led_9 (.in(cookiewatcher_5_cookiesburnt));
  LED led_10 (.in(cookiewatcher_5_cookiesdone));
  LED led_11 (.in(cookiewatcher_6_cookiesburnt));
  LED led_12 (.in(cookiewatcher_6_cookiesdone));
endmodule

module CookieWatcher (
  input  Clock,
  input  BatchHandled,
  output CookiesBurnt,
  output CookiesDone
);

  wire [8:0] counter_1_q;

  Counter #(.width(10), .max('h3ff), .ongoal("stay")) counter_1 (
    .load(1'b0), .count(1'b1), .Q({CookiesDone, counter_1_q}), .clk(Clock), .clr(BatchHandled));  // open: D, carry
  and and_1 (CookiesBurnt, counter_1_q[8], CookiesDone);
endmodule
